// Logisim project Exemplo_0704.circ as structural Verilog: 1 circuit, main circuit main
module main (
  input  [1:0] in_1,
  input  a,
  input  b,
  output s
);

  wire and_1_out, and_2_out, and_3_out, and_4_out, and_5_out, and_6_out, nor_1_out, not_1_out, not_2_out,
       or_1_out, or_2_out, or_3_out, xnor_1_out, xor_1_out;

  not not_1 (not_1_out, in_1[0]);
  or or_1 (or_1_out, b, a);
  nor nor_1 (nor_1_out, b, a);
  xor xor_1 (xor_1_out, b, a);
  xnor xnor_1 (xnor_1_out, a, b);
  and and_1 (and_1_out, or_1_out, not_1_out);
  or or_2 (or_2_out, and_1_out, and_2_out);
  and and_2 (and_2_out, in_1[0], nor_1_out);
  and and_3 (and_3_out, xor_1_out, not_1_out);
  or or_3 (or_3_out, and_3_out, and_4_out);
  and and_4 (and_4_out, in_1[0], xnor_1_out);
  not not_2 (not_2_out, in_1[1]);
  and and_5 (and_5_out, or_2_out, not_2_out);
  and and_6 (and_6_out, in_1[1], or_3_out);
  or or_4 (s, and_5_out, and_6_out);
endmodule
