// Logisim project Mealy_1101.circ as structural Verilog: 1 circuit, main circuit main
module main (
  input  in_1
);

  wire Clock, d_ff_1_qn, d_ff_2_q, d_ff_2_qn, or_1_out;

  D_Flip_Flop d_ff_1 (.clk(Clock), .D(d_ff_2_q), .Qn(d_ff_1_qn), .reset(in_1));  // open: Q, preset, en
  Clock clock_1 (.out(Clock));
  or or_1 (or_1_out, d_ff_1_qn, d_ff_2_qn);
  D_Flip_Flop d_ff_2 (.clk(Clock), .D(or_1_out), .Q(d_ff_2_q), .Qn(d_ff_2_qn), .reset(in_1));  // open: preset, en
endmodule
