// Logisim project Exemplo_1205.circ as structural Verilog: 6 circuits, main circuit main
module main (
  input  [2:0] Addr,
  input  R_W,
  input  CLK,
  input  [7:0] IN,
  input  CLR,
  output [7:0] out_6
);

  _8x8 u_8x8_1 (.Addr(Addr), .R_W(R_W), .CLK(CLK), .IN(IN), .out_6(out_6), .CLR(CLR));

  // Notes on the sheet:
  //   OUT
endmodule

module _1x4 (
  input  Addr,
  input  R_W,
  input  CLK,
  input  [3:0] IN,
  input  CLR,
  output [3:0] OUT
);

  _1x2 u_1x2_1 (.Addr(Addr), .R_W(R_W), .CLK(CLK), .IN(IN[1:0]), .OUT(OUT[1:0]), .CLR(CLR));
  _1x2 u_1x2_2 (.Addr(Addr), .R_W(R_W), .CLK(CLK), .IN(IN[3:2]), .OUT(OUT[3:2]), .CLR(CLR));
endmodule

module _1x2 (
  input  Addr,
  input  R_W,
  input  CLK,
  input  [1:0] IN,
  input  CLR,
  output [1:0] OUT
);

  wire ARC, j_k_ff_1_q, j_k_ff_2_q, not_1_out, not_2_out;

  and and_1 (ARC, Addr, R_W, CLK);
  J_K_Flip_Flop j_k_ff_1 (.J(IN[0]), .clk(ARC), .K(not_1_out), .Q(j_k_ff_1_q), .reset(CLR));  // open: Qn, preset, en
  not not_1 (not_1_out, IN[0]);
  J_K_Flip_Flop j_k_ff_2 (.J(IN[1]), .clk(ARC), .K(not_2_out), .Q(j_k_ff_2_q), .reset(CLR));  // open: Qn, preset, en
  not not_2 (not_2_out, IN[1]);
  and and_2 (OUT[0], Addr, j_k_ff_1_q);
  and and_3 (OUT[1], Addr, j_k_ff_2_q);
endmodule

module _1x8 (
  input  Addr,
  input  R_W,
  input  CLK,
  input  [7:0] in_4,
  input  CLR,
  output [7:0] out_6
);

  _1x4 u_1x4_1 (.R_W(R_W), .CLK(CLK), .IN(in_4[3:0]), .OUT(out_6[3:0]), .CLR(CLR), .Addr(Addr));
  _1x4 u_1x4_2 (.R_W(R_W), .CLK(CLK), .IN(in_4[7:4]), .OUT(out_6[7:4]), .CLR(CLR), .Addr(Addr));

  // Notes on the sheet:
  //   IN
endmodule

module _4x8 (
  input  [1:0] Addr,
  input  R_W,
  input  CLK,
  input  [7:0] IN,
  input  CLR,
  output [7:0] out_6
);

  wire demultiplexer_1_out0, demultiplexer_1_out1, demultiplexer_1_out2, demultiplexer_1_out3;
  wire [7:0] n1x8_1_out_6, n1x8_2_out_6, n1x8_3_out_6, n1x8_4_out_6;

  Demultiplexer #(.select(2)) demultiplexer_1 (
    .out0(demultiplexer_1_out0), .out1(demultiplexer_1_out1), .out2(demultiplexer_1_out2),
    .out3(demultiplexer_1_out3), .in(1'b1), .sel(Addr));  // open: en
  _1x8 u_1x8_1 (.Addr(demultiplexer_1_out0), .R_W(R_W), .CLK(CLK), .in_4(IN), .out_6(n1x8_1_out_6), .CLR(CLR));
  _1x8 u_1x8_2 (.Addr(demultiplexer_1_out1), .R_W(R_W), .CLK(CLK), .in_4(IN), .out_6(n1x8_2_out_6), .CLR(CLR));
  _1x8 u_1x8_3 (.Addr(demultiplexer_1_out2), .R_W(R_W), .CLK(CLK), .in_4(IN), .out_6(n1x8_3_out_6), .CLR(CLR));
  _1x8 u_1x8_4 (.Addr(demultiplexer_1_out3), .R_W(R_W), .CLK(CLK), .in_4(IN), .out_6(n1x8_4_out_6), .CLR(CLR));
  Multiplexer #(.select(2), .width(8)) multiplexer_1 (
    .in0(n1x8_1_out_6), .in1(n1x8_2_out_6), .in2(n1x8_3_out_6), .in3(n1x8_4_out_6), .out(out_6), .sel(Addr));  // open: en

  // Notes on the sheet:
  //   OUT
endmodule

module _8x8 (
  input  [2:0] Addr,
  input  R_W,
  input  CLK,
  input  [7:0] IN,
  input  CLR,
  output [7:0] out_6
);

  wire [1:0] demultiplexer_1_out0, demultiplexer_1_out1;
  wire [7:0] n4x8_1_out_6, n4x8_2_out_6;

  Demultiplexer #(.width(2)) demultiplexer_1 (
    .out0(demultiplexer_1_out0), .out1(demultiplexer_1_out1), .in(Addr[1:0]), .sel(Addr[2]));  // open: en
  _4x8 u_4x8_1 (.Addr(demultiplexer_1_out0), .R_W(R_W), .CLK(CLK), .IN(IN), .out_6(n4x8_1_out_6), .CLR(CLR));
  _4x8 u_4x8_2 (.Addr(demultiplexer_1_out1), .R_W(R_W), .CLK(CLK), .IN(IN), .out_6(n4x8_2_out_6), .CLR(CLR));
  Multiplexer #(.width(8)) multiplexer_1 (
    .in0(n4x8_1_out_6), .in1(n4x8_2_out_6), .out(out_6), .sel(Addr[2]));  // open: en

  // Notes on the sheet:
  //   OUT
endmodule
