// Logisim project Exemplo_0701.circ as structural Verilog: 1 circuit, main circuit main
module main (
  input  a,
  input  b,
  output s0,
  output s1
);

  and and_1 (s0, b, a);
  or or_1 (s1, a, b);
endmodule
