// Logisim project Exemplo_0702.circ as structural Verilog: 1 circuit, main circuit main
module main (
  input  a,
  input  b,
  input  key,
  output s
);

  wire and_1_out, and_2_out, and_3_out, not_1_out, or_1_out;

  not not_1 (not_1_out, key);
  and and_1 (and_1_out, b, a);
  or or_1 (or_1_out, a, b);
  and and_2 (and_2_out, key, and_1_out);
  and and_3 (and_3_out, not_1_out, or_1_out);
  or or_2 (s, and_2_out, and_3_out);
endmodule
