// Logisim project Exemplo_801.circ as structural Verilog: 1 circuit, main circuit main
module main (
  input  [3:0] in_1,
  input  [3:0] B,
  output [4:0] R
);

  wire and_1_out, and_2_out, and_3_out, and_4_out, and_5_out, and_6_out, and_7_out, and_8_out, or_2_out,
       or_3_out, or_4_out, xor_1_out, xor_3_out, xor_5_out, xor_7_out;

  and and_1 (and_1_out, in_1[3], in_1[3]);
  or or_1 (R[4], and_1_out, and_2_out);
  xor xor_1 (xor_1_out, B[3], in_1[3]);
  and and_2 (and_2_out, xor_1_out, or_2_out);
  xor xor_2 (R[3], or_2_out, xor_1_out);
  and and_3 (and_3_out, B[2], in_1[2]);
  and and_4 (and_4_out, xor_3_out, or_3_out);
  or or_2 (or_2_out, and_3_out, and_4_out);
  xor xor_3 (xor_3_out, B[2], in_1[2]);
  xor xor_4 (R[2], or_3_out, xor_3_out);
  and and_5 (and_5_out, B[1], in_1[1]);
  xor xor_5 (xor_5_out, B[1], in_1[1]);
  and and_6 (and_6_out, xor_5_out, or_4_out);
  or or_3 (or_3_out, and_5_out, and_6_out);
  xor xor_6 (R[1], or_4_out, xor_5_out);
  and and_7 (and_7_out, B[0], in_1[0]);
  and and_8 (and_8_out, xor_7_out, 1'b0);
  or or_4 (or_4_out, and_7_out, and_8_out);
  xor xor_7 (xor_7_out, B[0], in_1[0]);
  xor xor_8 (R[0], 1'b0, xor_7_out);

  // Notes on the sheet:
  //   Cin
  //   A
  //   Cin
  //   Cin
  //   Cin
endmodule
