// Logisim project Exemplo_803.circ as structural Verilog: 1 circuit, main circuit main
module main (
  input  [3:0] in_1,
  input  [3:0] B,
  output out_3
);

  wire xnor_1_out, xnor_2_out, xnor_3_out, xnor_4_out;

  xnor xnor_1 (xnor_1_out, in_1[3], B[3]);
  xnor xnor_2 (xnor_2_out, in_1[2], B[2]);
  and and_1 (out_3, xnor_1_out, xnor_2_out, xnor_3_out, xnor_4_out);
  xnor xnor_3 (xnor_3_out, in_1[1], B[1]);
  xnor xnor_4 (xnor_4_out, in_1[0], B[0]);

  // Notes on the sheet:
  //   A
endmodule
