// Logisim project Exemplo_804.circ as structural Verilog: 1 circuit, main circuit main
module main (
  input  [3:0] in_1,
  input  [3:0] B,
  output out_3
);

  wire xor_1_out, xor_2_out, xor_3_out, xor_4_out;

  xor xor_1 (xor_1_out, in_1[3], B[3]);
  xor xor_2 (xor_2_out, in_1[2], B[2]);
  or or_1 (out_3, xor_1_out, xor_2_out, xor_3_out, xor_4_out);
  xor xor_3 (xor_3_out, in_1[1], B[1]);
  xor xor_4 (xor_4_out, in_1[0], B[0]);

  // Notes on the sheet:
  //   A
endmodule
