// Logisim project Exemplo_1201.circ as structural Verilog: 2 circuits, main circuit main
module main (
  input  Addr,
  input  R_W,
  input  CLK,
  input  [3:0] IN,
  input  CLR,
  output [3:0] OUT
);

  _1x4 u_1x4_1 (.Addr(Addr), .R_W(R_W), .CLK(CLK), .IN(IN), .OUT(OUT), .CLR(CLR));
endmodule

module _1x4 (
  input  Addr,
  input  R_W,
  input  CLK,
  input  [3:0] IN,
  input  CLR,
  output [3:0] OUT
);

  wire ARC, j_k_ff_1_q, j_k_ff_2_q, j_k_ff_3_q, j_k_ff_4_q, not_1_out, not_2_out, not_3_out, not_4_out;

  and and_1 (ARC, Addr, R_W, CLK);
  not not_1 (not_1_out, IN[0]);
  J_K_Flip_Flop j_k_ff_1 (.J(IN[0]), .clk(ARC), .K(not_1_out), .Q(j_k_ff_1_q), .reset(CLR));  // open: Qn, preset, en
  J_K_Flip_Flop j_k_ff_2 (.J(IN[1]), .clk(ARC), .K(not_2_out), .Q(j_k_ff_2_q), .reset(CLR));  // open: Qn, preset, en
  not not_2 (not_2_out, IN[1]);
  J_K_Flip_Flop j_k_ff_3 (.J(IN[2]), .clk(ARC), .K(not_3_out), .Q(j_k_ff_3_q), .reset(CLR));  // open: Qn, preset, en
  not not_3 (not_3_out, IN[2]);
  J_K_Flip_Flop j_k_ff_4 (.J(IN[3]), .clk(ARC), .K(not_4_out), .Q(j_k_ff_4_q), .reset(CLR));  // open: Qn, preset, en
  not not_4 (not_4_out, IN[3]);
  and and_2 (OUT[0], Addr, j_k_ff_1_q);
  and and_3 (OUT[1], Addr, j_k_ff_2_q);
  and and_4 (OUT[2], Addr, j_k_ff_3_q);
  and and_5 (OUT[3], Addr, j_k_ff_4_q);
endmodule
