// Logisim project somadorCLA.circ as structural Verilog: 3 circuits, main circuit main
module _74LS83A (
  input  C0,
  input  A1,
  input  B1,
  input  A2,
  input  B2,
  input  A3,
  input  B3,
  input  A4,
  input  B4,
  output S1,
  output S2,
  output S3,
  output S4,
  output C4
);

  wire and_1_out, and_2_out, and_3_out, and_4_out, and_5_out, and_6_out, and_7_out, and_8_out, and_9_out,
       and_10_out, and_11_out, and_12_out, and_13_out, and_14_out, buffer_1_out, buffer_2_out, buffer_3_out,
       buffer_4_out, nand_1_out, nand_2_out, nand_3_out, nand_4_out, nor_1_out, nor_2_out, nor_3_out,
       nor_4_out, nor_5_out, nor_6_out, nor_7_out, not_1_out, not_2_out;

  not not_1 (not_1_out, C0);
  not not_2 (not_2_out, not_1_out);
  nor nor_1 (nor_1_out, A1, B1);
  and and_1 (and_1_out, ~nor_1_out, nand_1_out);  // AND_Gate
  xor xor_1 (S1, not_2_out, and_1_out);
  nand nand_1 (nand_1_out, A1, B1);
  and and_2 (and_2_out, not_1_out, nand_1_out);
  nor nor_2 (nor_2_out, and_2_out, buffer_1_out);
  nor nor_3 (nor_3_out, A2, B2);
  buf buffer_1 (buffer_1_out, nor_1_out);
  and and_3 (and_3_out, ~nor_3_out, nand_2_out);  // AND_Gate
  xor xor_2 (S2, nor_2_out, and_3_out);
  nand nand_2 (nand_2_out, A2, B2);
  and and_4 (and_4_out, not_1_out, nand_1_out, nand_2_out);
  buf buffer_2 (buffer_2_out, nor_3_out);
  and and_5 (and_5_out, nand_2_out, nor_1_out);
  nor nor_4 (nor_4_out, and_4_out, and_5_out, buffer_2_out);
  xor xor_3 (S3, nor_4_out, and_6_out);
  nand nand_3 (nand_3_out, A3, B3);
  nor nor_5 (nor_5_out, A3, B3);
  and and_6 (and_6_out, ~nor_5_out, nand_3_out);  // AND_Gate
  and and_7 (and_7_out, not_1_out, nand_1_out, nand_2_out, nand_3_out);
  and and_8 (and_8_out, nand_3_out, nor_3_out);
  and and_9 (and_9_out, nand_2_out, nand_3_out, nor_1_out);
  nor nor_6 (nor_6_out, and_7_out, and_9_out, and_8_out, buffer_3_out);
  nor nor_7 (nor_7_out, A4, B4);
  buf buffer_3 (buffer_3_out, nor_5_out);
  xor xor_4 (S4, nor_6_out, and_11_out);
  nand nand_4 (nand_4_out, A4, B4);
  and and_10 (and_10_out, not_1_out, nand_1_out, nand_2_out, nand_3_out, nand_4_out);
  and and_11 (and_11_out, ~nor_7_out, nand_4_out);  // AND_Gate
  and and_12 (and_12_out, nand_2_out, nand_3_out, nand_4_out, nor_1_out);
  and and_13 (and_13_out, nand_3_out, nand_4_out, nor_3_out);
  ExactlyOne xor_5 (
    .out(C4), .in0(and_10_out), .in1(and_12_out), .in2(and_13_out), .in3(and_14_out), .in4(buffer_4_out));
  and and_14 (and_14_out, nand_4_out, nor_5_out);
  buf buffer_4 (buffer_4_out, nor_7_out);
endmodule

module _74LS47 (
  input  D,
  input  C,
  input  B,
  input  A,
  output a_2,
  output b_2,
  output c_2,
  output d_2,
  output e,
  output f,
  output g
);

  wire and_1_out, and_2_out, and_3_out, and_4_out, and_5_out, and_6_out, and_7_out, and_8_out, and_9_out,
       and_10_out, and_11_out, and_12_out, and_13_out, and_14_out, and_15_out, and_16_out, and_17_out,
       not_1_out, not_2_out, not_3_out, not_4_out, not_5_out, not_6_out, not_7_out, not_8_out, not_9_out,
       not_10_out, not_11_out, not_12_out, not_13_out, not_14_out, not_15_out, not_16_out, not_17_out,
       not_18_out, not_19_out;

  not not_1 (not_1_out, D);
  not not_2 (not_2_out, C);
  not not_3 (not_3_out, B);
  not not_4 (not_4_out, A);
  not not_5 (not_5_out, B);
  and and_1 (and_1_out, C, not_5_out, A);
  and and_2 (and_2_out, C, B, not_6_out);
  not not_6 (not_6_out, A);
  and and_3 (and_3_out, D, B);
  not not_7 (not_7_out, C);
  and and_4 (and_4_out, not_7_out, B, not_8_out);
  not not_8 (not_8_out, A);
  and and_5 (and_5_out, D, C);
  not not_9 (not_9_out, C);
  not not_10 (not_10_out, B);
  and and_6 (and_6_out, not_9_out, not_10_out, A);
  not not_11 (not_11_out, B);
  and and_7 (and_7_out, C, not_11_out, not_12_out);
  not not_12 (not_12_out, A);
  and and_8 (and_8_out, C, B, A);
  and and_9 (and_9_out, C, not_13_out);
  not not_13 (not_13_out, B);
  not not_14 (not_14_out, D);
  not not_15 (not_15_out, C);
  and and_10 (and_10_out, not_14_out, not_15_out, A);
  not not_16 (not_16_out, C);
  and and_11 (and_11_out, not_16_out, B);
  and and_12 (and_12_out, B, A);
  not not_17 (not_17_out, D);
  not not_18 (not_18_out, C);
  and and_13 (and_13_out, not_17_out, not_18_out, not_19_out);
  not not_19 (not_19_out, B);
  and and_14 (and_14_out, C, B, A);
  and and_15 (and_15_out, not_1_out, not_2_out, not_3_out, A);
  and and_16 (and_16_out, C, not_4_out);
  and and_17 (and_17_out, D, B);
  nor nor_1 (b_2, and_1_out, and_2_out, and_3_out);
  nor nor_2 (c_2, and_4_out, and_5_out);
  nor nor_3 (d_2, and_6_out, and_7_out, and_8_out);
  nor nor_4 (e, A, and_9_out);
  nor nor_5 (f, and_10_out, and_11_out, and_12_out);
  nor nor_6 (g, and_13_out, and_14_out);
  nor nor_7 (a_2, and_15_out, and_16_out, and_17_out);
endmodule

module main (
  input  in_1,
  input  in_2,
  input  in_3,
  input  in_4,
  input  in_5,
  input  in_6,
  input  in_7,
  input  in_8,
  input  in_9,
  output out_10
);

  wire n74ls47_1_a_2, n74ls47_1_b_2, n74ls47_1_c_2, n74ls47_1_d_2, n74ls47_1_e, n74ls47_1_f, n74ls47_1_g,
       n74ls47_2_a_2, n74ls47_2_b_2, n74ls47_2_c_2, n74ls47_2_d_2, n74ls47_2_e, n74ls47_2_f, n74ls47_2_g,
       n74ls47_3_a_2, n74ls47_3_b_2, n74ls47_3_c_2, n74ls47_3_d_2, n74ls47_3_e, n74ls47_3_f, n74ls47_3_g,
       n74ls83a_1_s1, n74ls83a_1_s2, n74ls83a_1_s3, n74ls83a_1_s4;

  _74LS47 u_74ls47_1 (
    .D(in_1), .C(in_2), .B(in_3), .A(in_4), .a_2(n74ls47_1_a_2), .b_2(n74ls47_1_b_2), .c_2(n74ls47_1_c_2),
    .d_2(n74ls47_1_d_2), .e(n74ls47_1_e), .f(n74ls47_1_f), .g(n74ls47_1_g));
  _74LS47 u_74ls47_2 (
    .D(in_6), .C(in_7), .B(in_8), .A(in_9), .a_2(n74ls47_2_a_2), .b_2(n74ls47_2_b_2), .c_2(n74ls47_2_c_2),
    .d_2(n74ls47_2_d_2), .e(n74ls47_2_e), .f(n74ls47_2_f), .g(n74ls47_2_g));
  _7_Segment_Display u_7_segment_display_1 (
    .g(n74ls47_1_g), .f(n74ls47_1_f), .a(n74ls47_1_a_2), .b(n74ls47_1_b_2), .e(n74ls47_1_e),
    .d(n74ls47_1_d_2), .c(n74ls47_1_c_2), .dp(1'b0));
  _74LS83A u_74ls83a_1 (
    .C0(in_5), .A1(in_4), .B1(in_9), .A2(in_3), .B2(in_8), .A3(in_2), .B3(in_7), .A4(in_1), .B4(in_6),
    .S1(n74ls83a_1_s1), .S2(n74ls83a_1_s2), .S3(n74ls83a_1_s3), .S4(n74ls83a_1_s4), .C4(out_10));
  _7_Segment_Display u_7_segment_display_2 (
    .g(n74ls47_2_g), .f(n74ls47_2_f), .a(n74ls47_2_a_2), .b(n74ls47_2_b_2), .e(n74ls47_2_e),
    .d(n74ls47_2_d_2), .c(n74ls47_2_c_2), .dp(1'b0));
  _7_Segment_Display u_7_segment_display_3 (
    .g(n74ls47_3_g), .f(n74ls47_3_f), .a(n74ls47_3_a_2), .b(n74ls47_3_b_2), .e(n74ls47_3_e),
    .d(n74ls47_3_d_2), .c(n74ls47_3_c_2), .dp(1'b0));
  _74LS47 u_74ls47_3 (
    .D(n74ls83a_1_s4), .C(n74ls83a_1_s3), .B(n74ls83a_1_s2), .A(n74ls83a_1_s1), .a_2(n74ls47_3_a_2),
    .b_2(n74ls47_3_b_2), .c_2(n74ls47_3_c_2), .d_2(n74ls47_3_d_2), .e(n74ls47_3_e), .f(n74ls47_3_f),
    .g(n74ls47_3_g));

  // Notes on the sheet:
  //   +
  //   =
endmodule
