// Logisim project somador.circ as structural Verilog: 3 circuits, main circuit fulladder-4bits
module half_adder (
  input  A0,
  input  B0,
  output S0,
  output Cout
);

  xor xor_1 (S0, A0, B0);
  and and_1 (Cout, A0, B0);
endmodule

module fulladder_1bit (
  input  in_1,
  input  in_2,
  input  in_3,
  output out_4,
  output out_5
);

  wire half_adder_1_cout, half_adder_1_s0, half_adder_2_cout;

  half_adder half_adder_1 (.A0(in_2), .B0(in_3), .S0(half_adder_1_s0), .Cout(half_adder_1_cout));
  half_adder half_adder_2 (.A0(in_1), .B0(half_adder_1_s0), .S0(out_4), .Cout(half_adder_2_cout));
  or or_1 (out_5, half_adder_2_cout, half_adder_1_cout);
endmodule

module fulladder_4bits (
  input  Cin,
  input  A3,
  input  A2,
  input  A1,
  input  A0,
  input  B3,
  input  B2,
  input  B1,
  input  B0,
  output S3,
  output S2,
  output S1,
  output S0
);

  wire fulladder_1bit_1_out_5, fulladder_1bit_2_out_5, fulladder_1bit_3_out_5;

  fulladder_1bit fulladder_1bit_1 (.in_2(A0), .in_3(B0), .out_4(S0), .out_5(fulladder_1bit_1_out_5), .in_1(Cin));
  fulladder_1bit fulladder_1bit_2 (
    .in_2(A1), .in_3(B1), .out_4(S1), .out_5(fulladder_1bit_2_out_5), .in_1(fulladder_1bit_1_out_5));
  fulladder_1bit fulladder_1bit_3 (
    .in_2(A2), .in_3(B2), .out_4(S2), .out_5(fulladder_1bit_3_out_5), .in_1(fulladder_1bit_2_out_5));
  fulladder_1bit fulladder_1bit_4 (.in_2(A3), .in_3(B3), .out_4(S3), .in_1(fulladder_1bit_3_out_5));  // open: out_5
endmodule
