// Logisim project somadorCLA.circ as structural Verilog: 1 circuit, main circuit main
module main (
  input  C0,
  input  B0,
  input  A1,
  input  B1,
  input  A2,
  input  B2,
  input  A3,
  input  B3,
  input  A0
);

  // NOT_Gate not_1 is placed but not wired
  // NAND_Gate nand_1 is placed but not wired
  // NOR_Gate nor_1 is placed but not wired
  // NAND_Gate nand_2 has open pins: in0=A1, in1=B1, out=open
  // NOR_Gate nor_2 has open pins: in0=A1, in1=B1, out=open
  // NOR_Gate nor_3 has open pins: in0=A2, in1=B2, out=open
  // NAND_Gate nand_3 has open pins: in0=A2, in1=B2, out=open
  // NOR_Gate nor_4 has open pins: in0=A3, in1=B3, out=open
  // NAND_Gate nand_4 has open pins: in0=A3, in1=B3, out=open
endmodule
