// Logisim project unidade_logica_aritimetica.circ as structural Verilog: 8 circuits, main circuit ALU-4bits
module half_adder (
  input  A0,
  input  B0,
  output S0,
  output Cout
);

  xor xor_1 (S0, A0, B0);
  and and_1 (Cout, A0, B0);
endmodule

module fulladder_1bit (
  input  in_1,
  input  in_2,
  input  in_3,
  output out_4,
  output out_5
);

  wire half_adder_1_cout, half_adder_1_s0, half_adder_2_cout;

  half_adder half_adder_1 (.A0(in_2), .B0(in_3), .S0(half_adder_1_s0), .Cout(half_adder_1_cout));
  half_adder half_adder_2 (.A0(in_1), .B0(half_adder_1_s0), .S0(out_4), .Cout(half_adder_2_cout));
  or or_1 (out_5, half_adder_2_cout, half_adder_1_cout);
endmodule

module fulladder_4bits (
  input  Cin,
  input  A3,
  input  A2,
  input  A1,
  input  A0,
  input  B3,
  input  B2,
  input  B1,
  input  B0,
  output S3,
  output S2,
  output S1,
  output S0
);

  wire fulladder_1bit_1_out_5, fulladder_1bit_2_out_5, fulladder_1bit_3_out_5;

  fulladder_1bit fulladder_1bit_1 (.in_2(A0), .in_3(B0), .out_4(S0), .out_5(fulladder_1bit_1_out_5), .in_1(Cin));
  fulladder_1bit fulladder_1bit_2 (
    .in_2(A1), .in_3(B1), .out_4(S1), .out_5(fulladder_1bit_2_out_5), .in_1(fulladder_1bit_1_out_5));
  fulladder_1bit fulladder_1bit_3 (
    .in_2(A2), .in_3(B2), .out_4(S2), .out_5(fulladder_1bit_3_out_5), .in_1(fulladder_1bit_2_out_5));
  fulladder_1bit fulladder_1bit_4 (.in_2(A3), .in_3(B3), .out_4(S3), .in_1(fulladder_1bit_3_out_5));  // open: out_5
endmodule

module ALU_1bit (
  input  A,
  input  B,
  input  Op1,
  input  Op0,
  input  Binvert,
  input  Cin,
  output S,
  output Cout
);

  wire and_1_out, fulladder_1bit_1_out_4, multiplexador_2x1_1_c, not_1_out, not_2_out, or_1_out;

  not not_1 (not_1_out, A);
  not not_2 (not_2_out, B);
  multiplexador_2x1 multiplexador_2x1_1 (.A(B), .B(not_2_out), .OP(Binvert), .C(multiplexador_2x1_1_c));
  and and_1 (and_1_out, A, B);
  or or_1 (or_1_out, A, B);
  fulladder_1bit fulladder_1bit_1 (
    .in_2(A), .in_3(multiplexador_2x1_1_c), .out_4(fulladder_1bit_1_out_4), .out_5(Cout), .in_1(Cin));
  multiplexador_4x2 multiplexador_4x2_1 (
    .X(and_1_out), .Y(or_1_out), .Z(not_1_out), .K(fulladder_1bit_1_out_4), .S(S), .Op1(Op1), .Op0(Op0));
endmodule

module multiplexador_4x2 (
  input  X,
  input  Y,
  input  Z,
  input  K,
  input  Op1,
  input  Op0,
  output S
);

  wire and_1_out, and_2_out, and_3_out, and_4_out, and_5_out, and_6_out, and_7_out, and_8_out, not_1_out,
       not_2_out, not_3_out, not_4_out, or_1_out, or_2_out;

  not not_1 (not_1_out, Op0);
  not not_2 (not_2_out, Op0);
  and and_1 (and_1_out, X, not_1_out);
  not not_3 (not_3_out, Op1);
  and and_2 (and_2_out, Y, Op0);
  not not_4 (not_4_out, Op1);
  and and_3 (and_3_out, Z, not_2_out);
  and and_4 (and_4_out, K, Op0);
  and and_5 (and_5_out, and_1_out, not_3_out);
  and and_6 (and_6_out, and_2_out, not_4_out);
  and and_7 (and_7_out, and_3_out, Op1);
  and and_8 (and_8_out, and_4_out, Op1);
  or or_1 (or_1_out, and_5_out, and_6_out);
  or or_2 (or_2_out, and_7_out, and_8_out);
  or or_3 (S, or_1_out, or_2_out);
endmodule

module ALU_4bits (
  input  Binvert,
  input  A3,
  input  A2,
  input  A1,
  input  A0,
  input  B3,
  input  B2,
  input  B1,
  input  B0,
  input  Op1,
  input  Op0,
  output S,
  output S2,
  output S1,
  output S0,
  output out_16,
  output Cout
);

  wire alu_1bit_1_cout, alu_1bit_2_cout, alu_1bit_3_cout;

  ALU_1bit alu_1bit_1 (
    .A(A0), .B(B0), .S(S0), .Cin(Binvert), .Cout(alu_1bit_1_cout), .Op1(Op1), .Op0(Op0), .Binvert(Binvert));
  ALU_1bit alu_1bit_2 (
    .A(A1), .B(B1), .S(S1), .Cin(alu_1bit_1_cout), .Cout(alu_1bit_2_cout), .Op1(Op1), .Op0(Op0),
    .Binvert(Binvert));
  ALU_1bit alu_1bit_3 (
    .A(A2), .B(B2), .S(S2), .Cin(alu_1bit_2_cout), .Cout(alu_1bit_3_cout), .Op1(Op1), .Op0(Op0),
    .Binvert(Binvert));
  ALU_1bit alu_1bit_4 (
    .A(A3), .B(B3), .S(S), .Cin(alu_1bit_3_cout), .Cout(Cout), .Op1(Op1), .Op0(Op0), .Binvert(Binvert));
  xor xor_1 (out_16, alu_1bit_3_cout, Cout);
endmodule

module multiplexador_2x1 (
  input  A,
  input  B,
  input  OP,
  output C
);

  wire and_1_out, and_2_out, not_1_out;

  not not_1 (not_1_out, OP);
  and and_1 (and_1_out, B, OP);
  and and_2 (and_2_out, A, not_1_out);
  or or_1 (C, and_1_out, and_2_out);
endmodule

module ALU_2bits (
  input  Binvert,
  input  A1,
  input  A0,
  input  B1,
  input  B0,
  input  Op1,
  input  Op0,
  output S1,
  output S0,
  output Cout
);

  wire alu_1bit_1_cout;

  ALU_1bit alu_1bit_1 (
    .A(A0), .B(B0), .S(S0), .Cin(Binvert), .Cout(alu_1bit_1_cout), .Op1(Op1), .Op0(Op0), .Binvert(Binvert));
  ALU_1bit alu_1bit_2 (
    .A(A1), .B(B1), .S(S1), .Cin(alu_1bit_1_cout), .Cout(Cout), .Op1(Op1), .Op0(Op0), .Binvert(Binvert));
endmodule
